# Fritzing sketch Smart Salt Tunnel (saved by Fritzing 1.0.7)
breadboards: 1

parts:
  Arduino_UNO_R3 = Arduino Uno (Rev3) - ICSP
  MB-V2_(12V_DC_Input) = YwRobot Breadboard Power Supply [part_number=545043]
  DIY_Salinity_Sensor = PH meter [package=THT]
  HTU21D = Humidity Temperature Sensor SHT15
  DS18B20_Waterproof = DS18B20 1-Wire Temperature Sensor Probe
  Capacitor = Electrolytic Capacitor [capacitance=100μF voltage=35V package="0807 [SMD, electrolytic]"]
  NRF24L01 = NRF24L01
  TDS_Meter = tds-sensor-meter-v1.0_1
  Water_Level_Sensor1 = Water Level Sensor

nets:
  N1: Arduino_UNO_R3.A0, DIY_Salinity_Sensor.pin1
  N2: Arduino_UNO_R3.A1, TDS_Meter.pin1
  N3: Arduino_UNO_R3.A2, Water_Level_Sensor1.SIG
  N4: Arduino_UNO_R3.A4/SDA, HTU21D.SDA
  N5: Arduino_UNO_R3.A5/SCL, HTU21D.SCL
  GND: Arduino_UNO_R3.GND, MB-V2_(12V_DC_Input).GND, DIY_Salinity_Sensor.pin3, HTU21D.GND, DS18B20_Waterproof.GND, Capacitor.-, NRF24L01.GND, TDS_Meter.pin3, Water_Level_Sensor1.GND
  N6: Arduino_UNO_R3.D8, NRF24L01.CSN
  N7: Arduino_UNO_R3.D11_PWM/MOSI, NRF24L01.MOSI
  N8: Arduino_UNO_R3.D12/MISO, NRF24L01.MISO
  N9: Arduino_UNO_R3.D13/SCK, NRF24L01.SCK
  N10: Arduino_UNO_R3.D2, DS18B20_Waterproof.DQ
  N11: Arduino_UNO_R3.D7, NRF24L01.CE
  3V3: Arduino_UNO_R3.3V3, Capacitor.+, NRF24L01.VCC
  N12: Arduino_UNO_R3.VIN, MB-V2_(12V_DC_Input).VCC#9, MB-V2_(12V_DC_Input).VCC#10
  VCC: MB-V2_(12V_DC_Input).VCC#5, MB-V2_(12V_DC_Input).VCC#6, DIY_Salinity_Sensor.pin2, HTU21D.VCC, DS18B20_Waterproof.VDD, TDS_Meter.pin2, Water_Level_Sensor1.VCC

notes:
  +5V Bus

custom parts:
  YwRobot Breadboard Power Supply: The YwRobot Breadboard Power Supply (MB-V2) has two power rails; they can be 5V or 3V3. Power to the module can be provided through the female USB socket or through the A10 (female) 2.1mm power jack.
  : TDS Meter V1.0 Development Board Water Meter Filter Measuring Water Sensor Module.
  Water Level Sensor: A water level sensor. This sensor operates at 3V to 5V. The Sig (signal) pin outputs an analogue signal that is in proportion to the amount of water in contact with the sensor.
